// Logisim project Final Circuit.circ as structural Verilog: 7 circuits, main circuit main
module main (
  input  PC_Reset,
  input  RF_Reset,
  input  Memory_Reset
);

  wire ALU_Enable, Chip_Sel, clock_1_out, clock_2_out, clock_3_out, Data_DMUX_Sel, Decoder_Enable,
       Fetch_Enable, Mem_Address_MUX_Sel, Mem_Read_Write, Memory_Enable, MUX_B_Select, MUX_Y_Select, RF_Write;
  wire [4:0] id_1_destination, id_1_source_1, id_1_source_2;
  wire [5:0] Opcode_6;
  wire [31:0] alu_1_alu_output, demultiplexer_1_out0, demultiplexer_1_out1, fetch_unit_1_ir,
       fetch_unit_1_pc_address, id_1_immidiate_value, memory_1_data, multiplexer_1_out, multiplexer_2_out,
       multiplexer_3_out, register_1_q, register_2_q, register_file_1_output_a, register_file_1_output_b;

  Fetch_Unit fetch_unit_1 (
    .PC_Reset(PC_Reset), .PC_Address(fetch_unit_1_pc_address), .IR_Input(demultiplexer_1_out0),
    .IR(fetch_unit_1_ir), .Fetch_Enable(Fetch_Enable));
  ID id_1 (
    .Instruction(fetch_unit_1_ir), .Source_2(id_1_source_2), .Source_1(id_1_source_1),
    .Destination(id_1_destination), .Op_code(Opcode_6), .Immidiate_Value(id_1_immidiate_value));
  Register_File register_file_1 (
    .RF_CLR(RF_Reset), .Register_File_MUX_Enable(Decoder_Enable), .RF_WRITE(RF_Write),
    .Address_C(id_1_destination), .Address_B(id_1_source_2), .Address_A(id_1_source_1),
    .OUTPUT_B(register_file_1_output_b), .OUTPUT_A(register_file_1_output_a), .Input_Data(register_1_q));
  ALU alu_1 (
    .Input_A(register_file_1_output_a), .Input_B(multiplexer_1_out), .Opcode(Opcode_6),
    .ALU_OUTPUT(alu_1_alu_output), .ALU_MUX_ENABLE(ALU_Enable));
  Clock clock_1 (.out(clock_1_out));
  Multiplexer #(.width(32), .enable("false")) multiplexer_1 (
    .in0(register_file_1_output_b), .in1(id_1_immidiate_value), .out(multiplexer_1_out), .sel(MUX_B_Select));
  Multiplexer #(.width(32), .enable("false")) multiplexer_2 (
    .in0(alu_1_alu_output), .in1(demultiplexer_1_out1), .out(multiplexer_2_out), .sel(MUX_Y_Select));
  Register #(.width(32), .trigger("falling")) register_1 (
    .D(multiplexer_2_out), .en(Memory_Enable), .Q(register_1_q), .clk(clock_1_out));  // open: clr
  Clock clock_2 (.out(clock_2_out));
  Register #(.width(32), .trigger("falling")) register_2 (
    .D(register_file_1_output_b), .en(ALU_Enable), .Q(register_2_q), .clk(clock_2_out));  // open: clr
  Multiplexer #(.width(32), .enable("false")) multiplexer_3 (
    .in0(fetch_unit_1_pc_address), .in1(alu_1_alu_output), .out(multiplexer_3_out), .sel(Mem_Address_MUX_Sel));
  Demultiplexer #(.width(32), .enable("false")) demultiplexer_1 (
    .out0(demultiplexer_1_out0), .out1(demultiplexer_1_out1), .in(memory_1_data), .sel(Data_DMUX_Sel));
  Clock clock_3 (.out(clock_3_out));
  Memory memory_1 (
    .Memory_Address(multiplexer_3_out), .Memory(register_2_q), .Data(memory_1_data), .clk(clock_3_out),
    .Memory_Reset(Memory_Reset), .Read_Write(Mem_Read_Write), .Chip_Sel(Chip_Sel));
  Control_Unit control_unit_1 (
    .Opcode_6(Opcode_6), .Fetch_Enable(Fetch_Enable), .Chip_Sel(Chip_Sel), .Decode_Enable(Decoder_Enable),
    .ALU_ENABLE(ALU_Enable), .MUX_B_Select(MUX_B_Select), .Data_DMX_Sel(Mem_Address_MUX_Sel),
    .Memory_Address_MUX_Sel(Data_DMUX_Sel), .Memory_Enable(Memory_Enable), .MUX_Y_Select(MUX_Y_Select),
    .Mem_Read_Write(Mem_Read_Write), .RF_Write(RF_Write));

  // Notes on the sheet:
  //   Fetch Unit
  //   Instruction Decoder
  //   Register File
  //   ALU
  //   RZ
  //   RY
  //   Memory Unit
  //   Control Unit
endmodule

module Register_File (
  input  RF_CLR,
  input  Register_File_MUX_Enable,
  input  [31:0] Input_Data,
  input  RF_WRITE,
  input  [4:0] Address_B,
  input  [4:0] Address_A,
  input  [4:0] Address_C,
  output [31:0] OUTPUT_B,
  output [31:0] OUTPUT_A
);

  wire R1_en, R2_en, R3_en, R4_en, R5_en, R6_en, R7_en, R8_en, R9_en, R10_en, R11_en, R12_en, R13_en, R14_en,
       R15_en, R16_en, R17_en, R18_en, R19_en, R20_en, R21_en, R22_en, R23_en, R24_en, R25_en, R26_en,
       R27_en, R28_en, R29_en, R30_en, R31_en, R32_en, RA_RB_Clock;
  wire [31:0] multiplexer_1_out, multiplexer_2_out, R1_out, R2_out, R3_out, R4_out, R5_out, R6_out, R7_out,
       R8_out, R9_out, R10_out, R11_out, R12_out, R13_out, R14_out, R15_out, R16_out, R17_out, R18_out,
       R19_out, R20_out, R21_out, R22_out, R23_out, R24_out, R25_out, R26_out, R27_out, R28_out, R29_out,
       R30_out, R31_out, R32_out;

  Clock clock_1 (.out(RA_RB_Clock));
  Multiplexer #(.select(5), .width(32)) multiplexer_1 (
    .in0(R1_out), .in1(R2_out), .in2(R3_out), .in3(R4_out), .in4(R5_out), .in5(R6_out), .in6(R7_out),
    .in7(R8_out), .in8(R9_out), .in9(R10_out), .in10(R11_out), .in11(R12_out), .in12(R13_out),
    .in13(R14_out), .in14(R15_out), .in15(R16_out), .in16(R17_out), .in17(R18_out), .in18(R19_out),
    .in19(R20_out), .in20(R21_out), .in21(R22_out), .in22(R23_out), .in23(R24_out), .in24(R25_out),
    .in25(R26_out), .in26(R27_out), .in27(R28_out), .in28(R29_out), .in29(R30_out), .in30(R31_out),
    .in31(R32_out), .out(multiplexer_1_out), .sel(Address_B), .en(Register_File_MUX_Enable));
  Register #(.width(32), .trigger("falling")) register_1 (
    .D(Input_Data), .en(R1_en), .Q(R1_out), .clk(RA_RB_Clock), .clr(RF_CLR));
  Register #(.width(32), .trigger("falling")) register_2 (
    .D(Input_Data), .en(R9_en), .Q(R9_out), .clk(RA_RB_Clock), .clr(RF_CLR));
  Register #(.width(32), .trigger("falling")) register_3 (
    .D(Input_Data), .en(R17_en), .Q(R17_out), .clk(RA_RB_Clock), .clr(RF_CLR));
  Register #(.width(32), .trigger("falling")) register_4 (
    .D(Input_Data), .en(R25_en), .Q(R25_out), .clk(RA_RB_Clock), .clr(RF_CLR));
  Register #(.width(32), .trigger("falling")) RB (
    .D(multiplexer_1_out), .en(Register_File_MUX_Enable), .Q(OUTPUT_B), .clk(RA_RB_Clock));  // open: clr
  Register #(.width(32), .trigger("falling")) register_5 (
    .D(Input_Data), .en(R2_en), .Q(R2_out), .clk(RA_RB_Clock), .clr(RF_CLR));
  Register #(.width(32), .trigger("falling")) register_6 (
    .D(Input_Data), .en(R10_en), .Q(R10_out), .clk(RA_RB_Clock), .clr(RF_CLR));
  Register #(.width(32), .trigger("falling")) register_7 (
    .D(Input_Data), .en(R18_en), .Q(R18_out), .clk(RA_RB_Clock), .clr(RF_CLR));
  Register #(.width(32), .trigger("falling")) register_8 (
    .D(Input_Data), .en(R26_en), .Q(R26_out), .clk(RA_RB_Clock), .clr(RF_CLR));
  Register #(.width(32), .trigger("falling")) register_9 (
    .D(Input_Data), .en(R3_en), .Q(R3_out), .clk(RA_RB_Clock), .clr(RF_CLR));
  Register #(.width(32), .trigger("falling")) register_10 (
    .D(Input_Data), .en(R11_en), .Q(R11_out), .clk(RA_RB_Clock), .clr(RF_CLR));
  Register #(.width(32), .trigger("falling")) register_11 (
    .D(Input_Data), .en(R19_en), .Q(R19_out), .clk(RA_RB_Clock), .clr(RF_CLR));
  Register #(.width(32), .trigger("falling")) register_12 (
    .D(Input_Data), .en(R27_en), .Q(R27_out), .clk(RA_RB_Clock), .clr(RF_CLR));
  Register #(.width(32), .trigger("falling")) register_13 (
    .D(Input_Data), .en(R4_en), .Q(R4_out), .clk(RA_RB_Clock), .clr(RF_CLR));
  Register #(.width(32), .trigger("falling")) register_14 (
    .D(Input_Data), .en(R12_en), .Q(R12_out), .clk(RA_RB_Clock), .clr(RF_CLR));
  Register #(.width(32), .trigger("falling")) register_15 (
    .D(Input_Data), .en(R20_en), .Q(R20_out), .clk(RA_RB_Clock), .clr(RF_CLR));
  Register #(.width(32), .trigger("falling")) register_16 (
    .D(Input_Data), .en(R28_en), .Q(R28_out), .clk(RA_RB_Clock), .clr(RF_CLR));
  Multiplexer #(.select(5), .width(32)) multiplexer_2 (
    .in0(R1_out), .in1(R2_out), .in2(R3_out), .in3(R4_out), .in4(R5_out), .in5(R6_out), .in6(R7_out),
    .in7(R8_out), .in8(R9_out), .in9(R10_out), .in10(R11_out), .in11(R12_out), .in12(R13_out),
    .in13(R14_out), .in14(R15_out), .in15(R16_out), .in16(R17_out), .in17(R18_out), .in18(R19_out),
    .in19(R20_out), .in20(R21_out), .in21(R22_out), .in22(R23_out), .in23(R24_out), .in24(R25_out),
    .in25(R26_out), .in26(R27_out), .in27(R28_out), .in28(R29_out), .in29(R30_out), .in30(R31_out),
    .in31(R32_out), .out(multiplexer_2_out), .sel(Address_A), .en(Register_File_MUX_Enable));
  Register #(.width(32), .trigger("falling")) register_17 (
    .D(Input_Data), .en(R5_en), .Q(R5_out), .clk(RA_RB_Clock), .clr(RF_CLR));
  Register #(.width(32), .trigger("falling")) register_18 (
    .D(Input_Data), .en(R13_en), .Q(R13_out), .clk(RA_RB_Clock), .clr(RF_CLR));
  Register #(.width(32), .trigger("falling")) register_19 (
    .D(Input_Data), .en(R21_en), .Q(R21_out), .clk(RA_RB_Clock), .clr(RF_CLR));
  Register #(.width(32), .trigger("falling")) register_20 (
    .D(Input_Data), .en(R29_en), .Q(R29_out), .clk(RA_RB_Clock), .clr(RF_CLR));
  Register #(.width(32), .trigger("falling")) RA (
    .D(multiplexer_2_out), .en(Register_File_MUX_Enable), .Q(OUTPUT_A), .clk(RA_RB_Clock));  // open: clr
  Register #(.width(32), .trigger("falling")) register_21 (
    .D(Input_Data), .en(R6_en), .Q(R6_out), .clk(RA_RB_Clock), .clr(RF_CLR));
  Register #(.width(32), .trigger("falling")) register_22 (
    .D(Input_Data), .en(R14_en), .Q(R14_out), .clk(RA_RB_Clock), .clr(RF_CLR));
  Register #(.width(32), .trigger("falling")) register_23 (
    .D(Input_Data), .en(R22_en), .Q(R22_out), .clk(RA_RB_Clock), .clr(RF_CLR));
  Register #(.width(32), .trigger("falling")) register_24 (
    .D(Input_Data), .en(R30_en), .Q(R30_out), .clk(RA_RB_Clock), .clr(RF_CLR));
  Register #(.width(32), .trigger("falling")) register_25 (
    .D(Input_Data), .en(R7_en), .Q(R7_out), .clk(RA_RB_Clock), .clr(RF_CLR));
  Register #(.width(32), .trigger("falling")) register_26 (
    .D(Input_Data), .en(R15_en), .Q(R15_out), .clk(RA_RB_Clock), .clr(RF_CLR));
  Register #(.width(32), .trigger("falling")) register_27 (
    .D(Input_Data), .en(R23_en), .Q(R23_out), .clk(RA_RB_Clock), .clr(RF_CLR));
  Register #(.width(32), .trigger("falling")) register_28 (
    .D(Input_Data), .en(R31_en), .Q(R31_out), .clk(RA_RB_Clock), .clr(RF_CLR));
  Register #(.width(32), .trigger("falling")) register_29 (
    .D(Input_Data), .en(R8_en), .Q(R8_out), .clk(RA_RB_Clock), .clr(RF_CLR));
  Register #(.width(32), .trigger("falling")) register_30 (
    .D(Input_Data), .en(R16_en), .Q(R16_out), .clk(RA_RB_Clock), .clr(RF_CLR));
  Register #(.width(32), .trigger("falling")) register_31 (
    .D(Input_Data), .en(R24_en), .Q(R24_out), .clk(RA_RB_Clock), .clr(RF_CLR));
  Register #(.width(32), .trigger("falling")) register_32 (
    .D(Input_Data), .en(R32_en), .Q(R32_out), .clk(RA_RB_Clock), .clr(RF_CLR));
  Demultiplexer #(.select(5), .enable("false")) demultiplexer_1 (
    .out0(R1_en), .out1(R2_en), .out2(R3_en), .out3(R4_en), .out4(R5_en), .out5(R6_en), .out6(R7_en),
    .out7(R8_en), .out8(R9_en), .out9(R10_en), .out10(R11_en), .out11(R12_en), .out12(R13_en),
    .out13(R14_en), .out14(R15_en), .out15(R16_en), .out16(R17_en), .out17(R18_en), .out18(R19_en),
    .out19(R20_en), .out20(R21_en), .out21(R22_en), .out22(R23_en), .out23(R24_en), .out24(R25_en),
    .out25(R26_en), .out26(R27_en), .out27(R28_en), .out28(R29_en), .out29(R30_en), .out30(R31_en),
    .out31(R32_en), .in(RF_WRITE), .sel(Address_C));

  // Other names for the same wires on the sheet: R1_in[31:0] = Input_Data; R2_in[31:0] = Input_Data;
  //   R3_in[31:0] = Input_Data; R4_in[31:0] = Input_Data; R5_in[31:0] = Input_Data; R6_in[31:0] = Input_Data;
  //   R7_in[31:0] = Input_Data; R8_in[31:0] = Input_Data; R9_in[31:0] = Input_Data; R10_in[31:0] = Input_Data;
  //   R11_in[31:0] = Input_Data; R12_in[31:0] = Input_Data; R13_in[31:0] = Input_Data; R14_in[31:0] = Input_Data;
  //   R15_in[31:0] = Input_Data; R16_in[31:0] = Input_Data; R17_in[31:0] = Input_Data; R18_in[31:0] = Input_Data;
  //   R19_in[31:0] = Input_Data; R20_in[31:0] = Input_Data; R21_in[31:0] = Input_Data; R22_in[31:0] = Input_Data;
  //   R23_in[31:0] = Input_Data; R24_in[31:0] = Input_Data; R25_in[31:0] = Input_Data; R26_in[31:0] = Input_Data;
  //   R27_in[31:0] = Input_Data; R28_in[31:0] = Input_Data; R29_in[31:0] = Input_Data; R30_in[31:0] = Input_Data;
  //   R31_in[31:0] = Input_Data; R32_in[31:0] = Input_Data; RF_MUX_ENABLE = Register_File_MUX_Enable
endmodule

module ALU (
  input  [31:0] Input_A,
  input  [31:0] Input_B,
  input  ALU_MUX_ENABLE,
  input  [5:0] Opcode,
  output [31:0] ALU_OUTPUT
);

  wire clock_1_out;
  wire [3:0] bitselector_1_out;
  wire [31:0] adder_1_out, and_1_out, multiplexer_1_out, or_1_out, subtractor_1_out;

  BitSelector #(.width(6), .group(4)) bitselector_1 (.in(Opcode), .out(bitselector_1_out), .sel(1'b0));
  Adder #(.width(32)) adder_1 (.a(Input_A), .b(Input_B), .out(adder_1_out));  // open: cin, cout
  Subtractor #(.width(32)) subtractor_1 (.a(Input_A), .b(Input_B), .out(subtractor_1_out));  // open: bin, bout
  assign and_1_out = Input_A & Input_B;  // AND_Gate and_1, 32 bits wide
  assign or_1_out = Input_B | Input_A;  // OR_Gate or_1, 32 bits wide
  Multiplexer #(.select(4), .width(32)) multiplexer_1 (
    .in0(Input_A), .in1(Input_B), .in2(adder_1_out), .in3(adder_1_out), .in4(subtractor_1_out),
    .in5(subtractor_1_out), .in6(and_1_out), .in7(and_1_out), .in8(or_1_out), .in9(or_1_out),
    .in10(adder_1_out), .in11(adder_1_out), .out(multiplexer_1_out), .sel(bitselector_1_out),
    .en(ALU_MUX_ENABLE));  // open: in12, in13, in14, in15
  Register #(.width(32), .trigger("falling")) register_1 (
    .D(multiplexer_1_out), .en(ALU_MUX_ENABLE), .Q(ALU_OUTPUT), .clk(clock_1_out));  // open: clr
  Clock clock_1 (.out(clock_1_out));
endmodule

module Fetch_Unit (
  input  Fetch_Enable,
  input  [31:0] IR_Input,
  input  PC_Reset,
  output [31:0] PC_Address,
  output [31:0] IR
);

  wire clock_1_out;
  wire [31:0] adder_1_out;

  Clock clock_1 (.out(clock_1_out));
  Register #(.width(32), .trigger("falling")) PC (
    .D(adder_1_out), .en(Fetch_Enable), .Q(PC_Address), .clk(clock_1_out), .clr(PC_Reset));
  Adder #(.width(32)) adder_1 (.a(PC_Address), .b(32'h1), .out(adder_1_out));  // open: cin, cout
  Register #(.width(32), .trigger("falling")) u_IR (
    .D(IR_Input), .en(Fetch_Enable), .Q(IR), .clk(clock_1_out));  // open: clr
endmodule

module Memory (
  input  [31:0] Memory_Address,
  input  clk,
  input  [31:0] Memory,
  input  Memory_Reset,
  input  Chip_Sel,
  input  Read_Write,
  output [31:0] Data
);

  wire not_1_out, not_2_out;
  wire [23:0] bitselector_1_out;

  BitSelector #(.width(32), .group(24)) bitselector_1 (.in(Memory_Address), .out(bitselector_1_out), .sel(1'b0));
  not not_1 (not_1_out, Read_Write);
  RAM #(.addrWidth(24), .dataWidth(32), .bus("separate")) ram_1 (
    .addr(bitselector_1_out), .din(Memory), .data(Data), .str(Read_Write), .sel(Chip_Sel), .clk(not_2_out),
    .ld(not_1_out), .clr(Memory_Reset));
  not not_2 (not_2_out, clk);
endmodule

module ID (
  input  [31:0] Instruction,
  output [31:0] Immidiate_Value,
  output [4:0] Source_1,
  output [4:0] Destination,
  output [5:0] Op_code,
  output [4:0] Source_2
);

  wire comparator_1_eq;

  Comparator #(.width(6)) comparator_1 (.a(Instruction[31:26]), .b(6'b001011), .eq(comparator_1_eq));  // open: gt, lt
  Multiplexer #(.width(5), .enable("false")) multiplexer_1 (
    .in0(Instruction[15:11]), .in1(Instruction[25:21]), .out(Source_2), .sel(comparator_1_eq));
  assign Immidiate_Value = {{16{1'b0}}, Instruction[15:0]};  // Bit_Extender bit_extender_1

  assign Destination = Instruction[25:21];
  assign Op_code = Instruction[31:26];
  assign Source_1 = Instruction[20:16];
endmodule

module Control_Unit (
  input  [5:0] Opcode_6,
  output Fetch_Enable,
  output Chip_Sel,
  output Decode_Enable,
  output ALU_ENABLE,
  output MUX_B_Select,
  output Data_DMX_Sel,
  output Memory_Address_MUX_Sel,
  output Memory_Enable,
  output MUX_Y_Select,
  output Mem_Read_Write,
  output RF_Write
);

  wire and_4_out, clock_1_out, cnt, comparator_6_eq, comparator_8_eq, comparator_9_eq, comparator_10_eq,
       comparator_11_eq, comparator_12_eq, or_2_out, Stage_5;
  wire [2:0] Main_Counter_q;
  wire [3:0] Opcode_4;

  Clock clock_1 (.out(clock_1_out));
  BitSelector #(.width(6), .group(4)) bitselector_1 (.in(Opcode_6), .out(Opcode_4), .sel(1'b0));
  Counter #(.width(3), .max('h4)) Main_Counter (
    .count(cnt), .Q(Main_Counter_q), .clk(clock_1_out));  // open: load, D, carry, clr
  nand nand_1 (cnt, Opcode_6[2], Opcode_6[3], Stage_5);
  Comparator #(.width(3)) comparator_1 (.a(Main_Counter_q), .b(3'b000), .eq(Fetch_Enable));  // open: gt, lt
  Comparator #(.width(3)) comparator_2 (.a(Main_Counter_q), .b(3'b001), .eq(Decode_Enable));  // open: gt, lt
  Comparator #(.width(3)) comparator_3 (.a(Main_Counter_q), .b(3'b010), .eq(ALU_ENABLE));  // open: gt, lt
  Comparator #(.width(3)) comparator_4 (.a(Main_Counter_q), .b(3'b011), .eq(Memory_Enable));  // open: gt, lt
  Comparator #(.width(3)) comparator_5 (.a(Main_Counter_q), .b(3'b100), .eq(Stage_5));  // open: gt, lt
  Comparator #(.width(4)) comparator_6 (.a(4'b1010), .b(Opcode_4), .eq(comparator_6_eq));  // open: gt, lt
  Comparator #(.width(4)) comparator_7 (.a(4'b1010), .b(Opcode_4), .eq(MUX_Y_Select));  // open: gt, lt
  or or_1 (MUX_B_Select, Opcode_6[0], comparator_6_eq);
  Comparator #(.width(4)) comparator_8 (.a(4'b1010), .b(Opcode_4), .eq(comparator_8_eq));  // open: gt, lt
  Comparator #(.width(4)) comparator_9 (.a(Opcode_4), .b(4'b1011), .eq(comparator_9_eq));  // open: gt, lt
  Comparator #(.width(4)) comparator_10 (.a(Opcode_4), .b(4'b1011), .eq(comparator_10_eq));  // open: gt, lt
  Comparator #(.width(4)) comparator_11 (.a(4'b1010), .b(Opcode_4), .eq(comparator_11_eq));  // open: gt, lt
  Comparator #(.width(4)) comparator_12 (.a(Opcode_4), .b(4'b1011), .eq(comparator_12_eq));  // open: gt, lt
  and and_1 (Data_DMX_Sel, ~Fetch_Enable, Memory_Enable);  // AND_Gate
  and and_2 (Mem_Read_Write, ~Fetch_Enable, ~comparator_8_eq, comparator_9_eq);  // AND_Gate
  and and_3 (RF_Write, Stage_5, ~comparator_10_eq);  // AND_Gate
  or or_2 (or_2_out, comparator_11_eq, comparator_12_eq);
  and and_4 (and_4_out, Memory_Enable, or_2_out);
  or or_3 (Chip_Sel, Fetch_Enable, and_4_out);

  assign Memory_Address_MUX_Sel = Data_DMX_Sel;

  // Other names for the same wires on the sheet: B0 = Opcode_6[0]; B1 = Opcode_6[1]; B2 = Opcode_6[2];
  //   B3 = Opcode_6[3]; Stage_1 = Fetch_Enable; Stage_2 = Decode_Enable; Stage_3 = ALU_ENABLE;
  //   Stage_4 = Memory_Enable
endmodule
